# Fritzing sketch Controlling LED by Button (saved by Fritzing 0.8.7b)
breadboards: 1

parts:
  KEY = Pushbutton [package="[THT]"]
  元件1 = SunFounder Uno R3
  R1 = Resistor [tolerance=±5% resistance=10k package=THT]
  C1 = Ceramic Capacitor [capacitance=100nF package="100 mil [THT, multilayer]"]

nets:
  N1: KEY.Pin_1, KEY.Pin_2, 元件1.5V
  N2: KEY.Pin_3, KEY.Pin_4, 元件1.D12/MISO, R1.Pin_1, C1.1
  N3: 元件1.GND, R1.Pin_0, C1.0

custom parts:
  SunFounder Uno R3: The SunFounder Uno is a microcontroller board based on the ATmega328 (datasheet). It has 14 digital input/output pins (of which 6 can be used as PWM outputs), 6 analog inputs, a 16 MHz ceramic resonator, a USB connection, a power jack, an ICSP header, and a reset button. It contains everything needed to support the microcontroller; simply connect it to a computer with a USB cable or power it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
