# Fritzing sketch Slide switch (saved by Fritzing 0.8.7b)
breadboards: 1

parts:
  元件1 = SunFounder Uno R3
  R1 = Resistor [tolerance=±5% resistance=10k package=THT]
  C1 = Ceramic Capacitor [capacitance=100nF package="100 mil [THT, multilayer]"]
  S1 = Toggle Switch [package=THT]
  LED1 = LED - 5mm [color="Red (633nm)" package="5 mm [THT]"]
  R2 = Resistor [tolerance=±5% resistance=220 package=THT]

nets:
  N1: 元件1.D12/MISO, R1.Pin_0, C1.0, S1.L2
  N2: 元件1.GND, R1.Pin_1, C1.1, LED1.cathode
  N3: 元件1.D6_PWM, R2.Pin_0
  N4: 元件1.5V, S1.COM
  N5: LED1.anode, R2.Pin_1

custom parts:
  SunFounder Uno R3: The SunFounder Uno is a microcontroller board based on the ATmega328 (datasheet). It has 14 digital input/output pins (of which 6 can be used as PWM outputs), 6 analog inputs, a 16 MHz ceramic resonator, a USB connection, a power jack, an ICSP header, and a reset button. It contains everything needed to support the microcontroller; simply connect it to a computer with a USB cable or power it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
