# Fritzing sketch relay (saved by Fritzing 0.8.7b)
breadboards: 1

parts:
  K1 = Relay [part_number=FRS1B-S package=THT]
  Q1 = NPN-Transistor [package="TO92 [THT]"]
  D1 = Rectifier Diode [part_number=1N4001 package="300 mil [THT]"]
  LED1 = LED - 5mm [color="Red (633nm)" package="5 mm [THT]"]
  元件1 = SunFounder Uno R3
  R3 = Resistor [tolerance=±5% resistance=1k package=THT]
  R2 = Resistor [tolerance=±5% resistance=220 package=THT]

nets:
  N1: K1.COIL1, Q1.C, D1.anode
  N2: K1.C1, K1.C2, K1.COIL2, D1.cathode, 元件1.5V
  N3: K1.B, R2.Pin_0
  N4: Q1.E, LED1.cathode, 元件1.GND
  N5: Q1.B, R3.Pin_0
  N6: LED1.anode, R2.Pin_1
  N7: 元件1.D8, R3.Pin_1

custom parts:
  SunFounder Uno R3: The Arduino Uno is a microcontroller board based on the ATmega328 (datasheet). It has 14 digital input/output pins (of which 6 can be used as PWM outputs), 6 analog inputs, a 16 MHz ceramic resonator, a USB connection, a power jack, an ICSP header, and a reset button. It contains everything needed to support the microcontroller; simply connect it to a computer with a USB cable or power it with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
