# Fritzing sketch 4n35 (saved by Fritzing 0.8.7b)
breadboards: 1

parts:
  LED1 = LED - 5mm [color="Red (633nm)" package="5 mm [THT]"]
  元件1 = SunFounder Uno R3
  R1 = Resistor [tolerance=±5% resistance=220 package=THT]
  R2 = Resistor [tolerance=±5% resistance=1k package=THT]
  U2 = 4N35 [package=THT]

nets:
  N1: LED1.cathode, U2.Pin_5
  N2: LED1.anode, R1.Pin_0
  N3: 元件1.GND, U2.Pin_4
  N4: 元件1.D7, U2.Pin_2
  N5: 元件1.5V, R1.Pin_1, R2.Pin_0
  N6: R2.Pin_1, U2.Pin_1

custom parts:
  SunFounder Uno R3: The SunFounder Uno is a microcontroller board based on the ATmega328 (datasheet). It has 14 digital input/output pins (of which 6 can be used as PWM outputs), 6 analog inputs, a 16 MHz ceramic resonator, a USB connection, a power jack, an ICSP header, and a reset button. It contains everything needed to support the microcontroller; simply connect it to a computer with a USB cable or power it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
  4N35: Optocoupler - keeps you from frying your stuff!
