# Fritzing sketch Dot-matrix(2) (saved by Fritzing 0.8.7b)
breadboards: 1

parts:
  U2 = 74HC595 [package="DIP16 [THT]"]
  元件1 = SunFounder Uno R3
  R7 = Resistor [tolerance=±5% resistance=220 package=THT]  # not connected
  R6 = Resistor [tolerance=±5% resistance=220 package=THT]  # not connected
  R1 = Resistor [tolerance=±5% resistance=220 package=THT]  # not connected
  R4 = Resistor [tolerance=±5% resistance=220 package=THT]  # not connected
  R3 = Resistor [tolerance=±5% resistance=220 package=THT]  # not connected
  R2 = Resistor [tolerance=±5% resistance=220 package=THT]  # not connected
  R5 = Resistor [tolerance=±5% resistance=220 package=THT]  # not connected
  R8 = Resistor [tolerance=±5% resistance=220 package=THT]  # not connected
  module1 = 788BS Dot matix  # not connected
  U1 = 74HC595 SMD [package="SO16 [SMD]"]

nets:
  GND: U2.GND, U2.OE, 元件1.GND, U1.GND, U1.OE
  N1: U2.Q7', U1.DS
  VCC: U2.MR, U2.VCC, 元件1.5V, U1.MR, U1.VCC
  N2: U2.SH_CP, 元件1.D12/MISO, U1.SH_CP
  N3: U2.ST_CP, 元件1.D8, U1.ST_CP
  N4: U2.DS, 元件1.D11_PWM/MOSI

custom parts:
  SunFounder Uno R3: The SunFounder Uno is a microcontroller board based on the ATmega328 (datasheet). It has 14 digital input/output pins (of which 6 can be used as PWM outputs), 6 analog inputs, a 16 MHz ceramic resonator, a USB connection, a power jack, an ICSP header, and a reset button. It contains everything needed to support the microcontroller; simply connect it to a computer with a USB cable or power it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
  788BS Dot matix: 788BS 8x8 dot matix from SunFounder
