# Fritzing sketch Dot-matrix(4) (saved by Fritzing 0.8.7b)
breadboards: 1

parts:
  U2 = 74HC595 [package="DIP16 [THT]"]
  元件1 = SunFounder Uno R3
  R7 = Resistor [tolerance=±5% resistance=220 package=THT]
  R6 = Resistor [tolerance=±5% resistance=220 package=THT]
  R1 = Resistor [tolerance=±5% resistance=220 package=THT]
  R4 = Resistor [tolerance=±5% resistance=220 package=THT]
  R3 = Resistor [tolerance=±5% resistance=220 package=THT]
  R2 = Resistor [tolerance=±5% resistance=220 package=THT]
  R5 = Resistor [tolerance=±5% resistance=220 package=THT]
  R8 = Resistor [tolerance=±5% resistance=220 package=THT]
  module1 = 788BS Dot matix
  U1 = 74HC595 SMD [package="SO16 [SMD]"]

nets:
  N1: U2.Q1, module1.P6
  N2: U2.Q2, module1.P5
  N3: U2.Q3, module1.P10
  N4: U2.Q4, module1.P3
  N5: U2.Q5, module1.P11
  N6: U2.Q6, module1.P15
  N7: U2.Q7, module1.P16
  GND: U2.GND, U2.OE, 元件1.GND, U1.GND, U1.OE
  N8: U2.Q7', U1.DS
  VCC: U2.MR, U2.VCC, 元件1.5V, U1.MR, U1.VCC
  N9: U2.SH_CP, 元件1.D12/MISO, U1.SH_CP
  N10: U2.ST_CP, 元件1.D8, U1.ST_CP
  N11: U2.DS, 元件1.D11_PWM/MOSI
  N12: U2.Q0, module1.P13
  N13: R7.Pin_0, module1.P4
  N14: R7.Pin_1, U1.Q0
  N15: R6.Pin_0, module1.P7
  N16: R6.Pin_1, U1.Q1
  N17: R1.Pin_0, module1.P2
  N18: R1.Pin_1, U1.Q2
  N19: R4.Pin_0, module1.P8
  N20: R4.Pin_1, U1.Q3
  N21: R3.Pin_0, module1.P12
  N22: R3.Pin_1, U1.Q4
  N23: R2.Pin_0, module1.P1
  N24: R2.Pin_1, U1.Q5
  N25: R5.Pin_0, module1.P14
  N26: R5.Pin_1, U1.Q6
  N27: R8.Pin_0, module1.P9
  N28: R8.Pin_1, U1.Q7

custom parts:
  SunFounder Uno R3: The SunFounder Uno is a microcontroller board based on the ATmega328 (datasheet). It has 14 digital input/output pins (of which 6 can be used as PWM outputs), 6 analog inputs, a 16 MHz ceramic resonator, a USB connection, a power jack, an ICSP header, and a reset button. It contains everything needed to support the microcontroller; simply connect it to a computer with a USB cable or power it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
  788BS Dot matix: 788BS 8x8 dot matix from SunFounder
