# Fritzing sketch ne555 (saved by Fritzing 0.8.7b)
breadboards: 1

parts:
  C1 = Ceramic Capacitor [capacitance=100nF package="100 mil [THT, multilayer]"]
  R1 = Rotary Potentiometer (Small) [maximum_resistance=100kΩ package=THT]
  R2 = Resistor [tolerance=±5% resistance=10k package=THT]
  C2 = Ceramic Capacitor [capacitance=100nF package="100 mil [THT, multilayer]"]
  元件2 = SunFounder Uno R3
  IC1 = Timer-NE555 [part_number=NE555 package=dil-08]

nets:
  GND: C1.0, C2.1, 元件2.GND, IC1.GND
  N1: C1.1, R1.leg1, IC1.TRI, IC1.TRE
  N2: R1.wiper, R2.Pin_1, IC1.DIS
  N3: R2.Pin_0, 元件2.5V, IC1._RES, IC1.VCC+
  N4: C2.0, IC1.CON
  N5: 元件2.D7, IC1.OUT

custom parts:
  SunFounder Uno R3: The SunFounder Uno is a microcontroller board based on the ATmega328 (datasheet). It has 14 digital input/output pins (of which 6 can be used as PWM outputs), 6 analog inputs, a 16 MHz ceramic resonator, a USB connection, a power jack, an ICSP header, and a reset button. It contains everything needed to support the microcontroller; simply connect it to a computer with a USB cable or power it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
  Timer-NE555: 555 Timer IC
