# Fritzing sketch ADXL335 (saved by Fritzing 0.8.7b)
breadboards: 1

parts:
  元件4 = SunFounder Uno R3
  元件5 = ADXL335 v1.0

nets:
  N1: 元件4.A0, 元件5.XOUT
  N2: 元件4.A1, 元件5.YOUT
  N3: 元件4.A2, 元件5.ZOUT
  GND: 元件4.GND, 元件5.GND
  5V: 元件4.5V, 元件5.VCC

custom parts:
  SunFounder Uno R3: The SunFounder Uno is a microcontroller board based on the ATmega328 (datasheet). It has 14 digital input/output pins (of which 6 can be used as PWM outputs), 6 analog inputs, a 16 MHz ceramic resonator, a USB connection, a power jack, an ICSP header, and a reset button. It contains everything needed to support the microcontroller; simply connect it to a computer with a USB cable or power it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
  ADXL335 v1.0: Accelerometer for sensing three-dimensional orientation/acceleration on a breakout board. Compatible to the ADXL3xx series of sensor chips.
