# Fritzing sketch Traffic Light (saved by Fritzing 0.8.7b)
breadboards: 1

parts:
  R4 = Resistor [tolerance=±5% resistance=220 package=THT]
  R5 = Resistor [tolerance=±5% resistance=220 package=THT]
  R8 = Resistor [tolerance=±5% resistance=220 package=THT]
  R7 = Resistor [tolerance=±5% resistance=220 package=THT]
  R6 = Resistor [tolerance=±5% resistance=220 package=THT]
  U1 = 74HC595 [package="DIP16 [THT]"]
  DI1 = 7-Segment LED Display [package=THT]
  R3 = Resistor [tolerance=±5% resistance=220 package=THT]
  元件1 = SunFounder Uno R3
  R2 = Resistor [tolerance=±5% resistance=220 package=THT]
  LED1 = LED - 5mm [color="Red (633nm)" package="5 mm [THT]"]
  LED2 = LED - 5mm [color="Red (633nm)" package="5 mm [THT]"]
  LED3 = LED - 5mm [color="Yellow (585nm)" package="5 mm [THT]"]
  LED4 = LED - 5mm [color="Yellow (585nm)" package="5 mm [THT]"]
  LED5 = LED - 5mm [color="Green (555nm)" package="5 mm [THT]"]
  LED6 = LED - 5mm [color="Green (555nm)" package="5 mm [THT]"]

nets:
  N1: R4.Pin_0, LED2.anode
  N2: R4.Pin_1, 元件1.D2
  N3: R5.Pin_0, LED3.anode
  N4: R5.Pin_1, 元件1.D6_PWM
  GND: R8.Pin_0, U1.GND, U1.OE, 元件1.GND, LED1.cathode, LED2.cathode, LED3.cathode, LED4.cathode, LED5.cathode, LED6.cathode
  N5: R8.Pin_1, DI1.commAnode#2
  N6: R7.Pin_0, LED1.anode
  N7: R7.Pin_1, 元件1.D5_PWM
  N8: R6.Pin_0, LED4.anode
  N9: R6.Pin_1, 元件1.D3_PWM
  N10: U1.Q1, DI1.cathodeG
  N11: U1.Q2, DI1.cathodeF
  N12: U1.Q3, DI1.cathodeE
  N13: U1.Q4, DI1.cathodeD
  N14: U1.Q5, DI1.cathodeC
  N15: U1.Q6, DI1.cathodeB
  N16: U1.Q7, DI1.cathodeA
  VCC: U1.MR, U1.VCC, 元件1.5V
  N17: U1.SH_CP, 元件1.D8
  N18: U1.ST_CP, 元件1.D12/MISO
  N19: U1.DS, 元件1.D11_PWM/MOSI
  N20: U1.Q0, DI1.cathodeDP
  N21: R3.Pin_0, LED5.anode
  N22: R3.Pin_1, 元件1.D7
  N23: 元件1.D4, R2.Pin_1
  N24: R2.Pin_0, LED6.anode

notes:
  North-south
  East-west

custom parts:
  SunFounder Uno R3: The SunFounder Uno is a microcontroller board based on the ATmega328 (datasheet). It has 14 digital input/output pins (of which 6 can be used as PWM outputs), 6 analog inputs, a 16 MHz ceramic resonator, a USB connection, a power jack, an ICSP header, and a reset button. It contains everything needed to support the microcontroller; simply connect it to a computer with a USB cable or power it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
