# Fritzing sketch Simple Creation - Digital Dice (saved by Fritzing 0.8.7b)
breadboards: 1

parts:
  U1 = 74HC595 [package="DIP16 [THT]"]
  DI1 = 7-Segment LED Display [package=THT]
  R8 = Resistor [tolerance=±5% resistance=220 package=THT]
  R6 = Resistor [tolerance=±5% resistance=220 package=THT]
  R1 = Resistor [tolerance=±5% resistance=220 package=THT]
  R4 = Resistor [tolerance=±5% resistance=220 package=THT]
  R2 = Resistor [tolerance=±5% resistance=220 package=THT]
  R7 = Resistor [tolerance=±5% resistance=220 package=THT]
  R5 = Resistor [tolerance=±5% resistance=220 package=THT]
  R3 = Resistor [tolerance=±5% resistance=220 package=THT]
  元件1 = SunFounder Uno R3
  R9 = Resistor [tolerance=±5% resistance=10k package=THT]
  C1 = Ceramic Capacitor [capacitance=100nF package="100 mil [THT, multilayer]"]
  S1 = Pushbutton [package="[THT]"]  # not connected

nets:
  N1: U1.Q1, R3.Pin_0
  N2: U1.Q2, R5.Pin_0
  N3: U1.Q3, R2.Pin_0
  N4: U1.Q5, R8.Pin_1
  N5: U1.Q6, R7.Pin_1
  N6: U1.Q7, R4.Pin_1
  GND: U1.GND, U1.OE, DI1.commAnode#2, 元件1.GND, R9.Pin_1, C1.1
  VCC: U1.MR, U1.VCC, 元件1.5V
  N7: U1.SH_CP, 元件1.D8
  N8: U1.ST_CP, 元件1.D12/MISO
  N9: U1.DS, 元件1.D11_PWM/MOSI
  N10: U1.Q0, R6.Pin_1
  N11: DI1.cathodeE, R2.Pin_1
  N12: DI1.cathodeD, R1.Pin_1
  N13: DI1.cathodeC, R8.Pin_0
  N14: DI1.cathodeDP, R6.Pin_0
  N15: DI1.cathodeB, R7.Pin_0
  N16: DI1.cathodeA, R4.Pin_0
  N17: DI1.cathodeF, R5.Pin_1
  N18: DI1.cathodeG, R3.Pin_1
  N19: 元件1.D2, R9.Pin_0, C1.0

custom parts:
  SunFounder Uno R3: The SunFounder Uno is a microcontroller board based on the ATmega328 (datasheet). It has 14 digital input/output pins (of which 6 can be used as PWM outputs), 6 analog inputs, a 16 MHz ceramic resonator, a USB connection, a power jack, an ICSP header, and a reset button. It contains everything needed to support the microcontroller; simply connect it to a computer with a USB cable or power it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
