# Fritzing sketch wakeupclock (saved by Fritzing 0.9.3b)
breadboards: 1

parts:
  Part1 = Arduino Uno (Rev3)
  Q1 = MOSFET-NCHANNEL [package=to220v]
  Part2 = Real Time Clock Module - DS1307 RTC Breakout Board
  Power_RGB1 = Prolight RGB 3 Watt Star

nets:
  N1: Part1.D9_PWM, Q1.G
  GND: Part1.GND, Q1.S, Part2.GND
  N2: Part1.A4/SDA, Part2.SDA
  N3: Part1.A5/SCL, Part2.SCL
  5V: Part1.5V, Part2.5V, Power_RGB1.B+
  N4: Q1.D, Power_RGB1.R-
